# Fritzing sketch domus-hub-breadboard-scheme (saved by Fritzing 0.9.4)
breadboards: 1

parts:
  LED5 = LED - 5mm [color="Green (565nm)" package="5 mm [THT]"]
  LED6 = LED - 5mm [color="Red (633nm)" package="5 mm [THT]"]
  Componente2 = Bluetooth HC-05 Macho  # not connected
  R3 = Resistor [tolerance=±5% resistance=220 package="0402 [SMD]"]
  LED7 = LED - 5mm [color="Yellow (595nm)" package="5 mm [THT]"]
  Componente1 = Arduino Uno (Rev3)
  Componente3 = LCD1602-I2C
  R13 = Resistor [tolerance=±5% resistance=220 package="0402 [SMD]"]
  R14 = Resistor [tolerance=±5% resistance=220 package="0402 [SMD]"]
  J1 = Basic Servo
  S2 = Momentary Switch [package=ksa_sealed_tac_switch]
  S1 = Momentary Switch [package=ksa_sealed_tac_switch]
  PIR2 = PIR sensor

nets:
  N1: LED5.cathode, Componente1.D12/MISO
  N2: LED5.anode, R13.Pin_0
  N3: LED6.cathode, Componente1.D13/SCK
  N4: LED6.anode, R3.Pin_0
  GND: R3.Pin_1, Componente1.GND, Componente3.GND, R13.Pin_1, R14.Pin_1, J1.gnd, S2.2, S1.2, PIR2.GND
  N5: LED7.cathode, Componente1.D11_PWM/MOSI
  N6: LED7.anode, R14.Pin_0
  N7: Componente1.D8, PIR2.SIG
  N8: Componente1.D9_PWM, S2.4
  N9: Componente1.D10_PWM/SS, S1.4
  N10: Componente1.D2, Componente3.SCL
  N11: Componente1.D3_PWM, Componente3.SDA
  N12: Componente1.D6_PWM, J1.pulse
  VCC: Componente1.5V, Componente3.VCC, J1.vcc, PIR2.VDD

custom parts:
  LCD1602-I2C: A standard character display, usually with 2x16 characters. Comes in many colors with LCM1602 IIC attached.
